# Fritzing sketch Sketch (saved by Fritzing 0.9.3b)
breadboards: 1

parts:
  LED1 = LED - 3mm [color="Yellow (585nm)" package="3 mm [THT]"]
  U1 = ESP32-38PinWide [part_number=ESP32-38PinWide]
  S3 = Pushbutton [package="[SMD]"]
  S4 = Pushbutton [package="[SMD]"]
  S5 = Pushbutton [package="[SMD]"]
  S6 = Pushbutton [package="[SMD]"]
  LED2 = LED - 3mm [color="Green (570nm)" package="3 mm [THT]"]
  LED3 = LED - 3mm [color="Red (633nm)" package="3 mm [THT]"]
  R1 = Resistor [tolerance=±5% resistance=220 package="0603 [SMD]"]
  R2 = Resistor [tolerance=±5% resistance=220 package="0603 [SMD]"]
  R4 = Resistor [tolerance=±5% resistance=220 package="0603 [SMD]"]
  R7 = Resistor [tolerance=±10% resistance=10k package=THT]
  R8 = Resistor [tolerance=±10% resistance=10k package=THT]
  R9 = Resistor [tolerance=±10% resistance=10k package=THT]
  R10 = Resistor [tolerance=±10% resistance=10k package=THT]

nets:
  N1: LED1.cathode, U1.GND, LED2.cathode, LED3.cathode, R7.Pin_1, R8.Pin_1, R9.Pin_1, R10.Pin_1
  N2: LED1.anode, R1.Pin_0
  N3: U1.VIN, S3.Pin_3, S3.Pin_4, S4.Pin_3, S4.Pin_4, S5.Pin_3, S5.Pin_4, S6.Pin_3, S6.Pin_4
  N4: U1.GPIO0, S4.Pin_1, S4.Pin_2, R7.Pin_0
  N5: U1.GPIO4, S5.Pin_1, S5.Pin_2, R8.Pin_0
  N6: U1.GPIO16, S6.Pin_1, S6.Pin_2, R10.Pin_0
  N7: U1.GPIO17, S3.Pin_1, S3.Pin_2, R9.Pin_0
  N8: U1.GPIO5, R2.Pin_1
  N9: U1.GPIO18, R1.Pin_1
  N10: U1.GPIO19, R4.Pin_1
  N11: LED2.anode, R2.Pin_0
  N12: LED3.anode, R4.Pin_0

custom parts:
  ESP32-38PinWide: Generic 38-Pin ESP32 with wide format (only access to one side of pins on a breadboard) based on Stephen Lilley's HiLetgo ESP-WROOM-32 ESP32 ESP-32S Development Board.
